# Fritzing sketch Fritzing Sketch Source File (saved by Fritzing 0.9.3b)
breadboards: 1

parts:
  Part1 = InvenSense MPU6050
  Part2 = Arduino Uno (Rev3)
  J1 = Basic Servo

nets:
  VCC: Part1.VCC, Part2.5V, J1.vcc
  GND: Part1.GND, Part1.AD0, Part2.GND, J1.gnd
  N1: Part1.SCL, Part2.A5/SCL
  N2: Part1.SDA, Part2.A4/SDA
  N3: Part1.INT, Part2.D2
  N4: Part2.D9_PWM, J1.pulse

notes:
  Developed By Web Dev Fusion
  https://www.webdevfusion.com
  GND - Green
  VCC - Orange
  GPIO - Blue
